// Logisim project microProcessor_frog.circ as structural Verilog: 2 circuits, main circuit main
module main (
);

  wire [1:0] undriven, undriven_2;
  wire [15:0] multiplexer_1_out, multiplexer_2_out, regbank_1_out_5, regbank_1_out_6, regbank_1_out_7,
       regbank_1_out_8;

  regbank regbank_1 (
    .out_5(regbank_1_out_5), .out_6(regbank_1_out_6), .out_7(regbank_1_out_7), .out_8(regbank_1_out_8));  // open: LD, REGSEL, Din, clock
  Multiplexer #(.select(2), .width(16), .enable("false")) multiplexer_1 (
    .in0(regbank_1_out_5), .in1(regbank_1_out_6), .in2(regbank_1_out_7), .in3(regbank_1_out_8),
    .out(multiplexer_1_out), .sel(undriven));
  Multiplexer #(.select(2), .width(16), .enable("false")) multiplexer_2 (
    .in0(regbank_1_out_5), .in1(regbank_1_out_6), .in2(regbank_1_out_7), .in3(regbank_1_out_8),
    .out(multiplexer_2_out), .sel(undriven_2));
endmodule

module regbank (
  input  LD,
  input  [1:0] REGSEL,
  input  [15:0] Din,
  input  clock,
  output [15:0] out_5,
  output [15:0] out_6,
  output [15:0] out_7,
  output [15:0] out_8
);

  wire and_1_out, and_2_out, and_3_out, and_4_out, decoder_1_out0, decoder_1_out1, decoder_1_out2,
       decoder_1_out3;

  Decoder #(.select(2)) decoder_1 (
    .out0(decoder_1_out0), .out1(decoder_1_out1), .out2(decoder_1_out2), .out3(decoder_1_out3), .sel(REGSEL));  // open: en
  and and_1 (and_1_out, decoder_1_out0, LD);
  and and_2 (and_2_out, decoder_1_out1, LD);
  and and_3 (and_3_out, decoder_1_out2, LD);
  and and_4 (and_4_out, decoder_1_out3, LD);
  Register #(.width(16)) register_1 (.D(Din), .en(and_1_out), .Q(out_5), .clk(clock));  // open: clr
  Register #(.width(16)) register_2 (.D(Din), .en(and_2_out), .Q(out_6), .clk(clock));  // open: clr
  Register #(.width(16)) register_3 (.D(Din), .en(and_3_out), .Q(out_7), .clk(clock));  // open: clr
  Register #(.width(16)) register_4 (.D(Din), .en(and_4_out), .Q(out_8), .clk(clock));  // open: clr
endmodule
